// Logisim project trafficlight8.0.circ as structural Verilog: 4 circuits, main circuit sevensements1
module main (
);

  wire and_1_out, and_2_out, and_3_out, and_4_out, and_5_out, and_6_out, clock_1_out, clock_2_out,
       comparator_1_eq, comparator_2_eq, comparator_3_eq, comparator_4_eq, comparator_4_gt, comparator_4_lt,
       comparator_5_eq, comparator_5_gt, comparator_5_lt, d_ff_1_q, d_ff_1_qn, not_1_out, not_2_out,
       or_1_out, or_2_out, sevensegment2_1_s1, sevensegment2_1_s2, sevensegment2_1_s3, sevensegment2_1_s4,
       sevensegment2_1_s5, sevensegment2_1_s6, sevensegment2_1_s7, sevensegment2_2_s1, sevensegment2_2_s2,
       sevensegment2_2_s3, sevensegment2_2_s4, sevensegment2_2_s5, sevensegment2_2_s6, sevensegment2_2_s7,
       sevensements1_1_s1, sevensements1_1_s2, sevensements1_1_s3, sevensements1_1_s4, sevensements1_1_s5,
       sevensements1_1_s6, sevensements1_1_s7, sevensements1_2_s1, sevensements1_2_s2, sevensements1_2_s3,
       sevensements1_2_s4, sevensements1_2_s5, sevensements1_2_s6, sevensements1_2_s7;
  wire [4:0] counter_1_q, counter_2_q, counter_3_q;

  D_Flip_Flop d_ff_1 (.D(d_ff_1_qn), .clk(comparator_3_eq), .Q(d_ff_1_q), .Qn(d_ff_1_qn));  // open: preset, reset
  Clock clock_1 (.out(clock_1_out));
  Counter #(.max('h1f), .width(5)) counter_1 (
    .clr(comparator_1_eq), .clk(and_1_out), .Q(counter_1_q));  // open: load, up, count, D, carry
  and and_1 (and_1_out, clock_1_out, d_ff_1_q);
  Counter #(.max('h1f), .width(5)) counter_2 (
    .clr(comparator_2_eq), .clk(and_2_out), .Q(counter_2_q));  // open: load, up, count, D, carry
  and and_2 (and_2_out, clock_1_out, d_ff_1_qn);
  Counter #(.max('h1e), .width(5)) counter_3 (
    .clr(comparator_3_eq), .clk(clock_2_out), .Q(counter_3_q));  // open: load, up, count, D, carry
  Clock clock_2 (.out(clock_2_out));
  Comparator #(.mode("unsigned"), .width(5)) comparator_1 (
    .a({5{1'b1}}), .b(counter_1_q), .eq(comparator_1_eq));  // open: gt, lt
  Comparator #(.mode("unsigned"), .width(5)) comparator_2 (
    .a({5{1'b1}}), .b(counter_2_q), .eq(comparator_2_eq));  // open: gt, lt
  Comparator #(.width(5)) comparator_3 (.a(5'b11110), .b(counter_3_q), .eq(comparator_3_eq));  // open: gt, lt
  sevensements1 sevensements1_1 (
    .i1(counter_1_q[4]), .i2(counter_1_q[3]), .i3(counter_1_q[2]), .i4(counter_1_q[1]), .i5(counter_1_q[0]),
    .s1(sevensements1_1_s1), .s2(sevensements1_1_s2), .s3(sevensements1_1_s3), .s4(sevensements1_1_s4),
    .s5(sevensements1_1_s5), .s6(sevensements1_1_s6), .s7(sevensements1_1_s7));
  sevensegment2 sevensegment2_1 (
    .a(counter_1_q[4]), .b(counter_1_q[3]), .c(counter_1_q[2]), .d(counter_1_q[1]), .e(counter_1_q[0]),
    .s1(sevensegment2_1_s1), .s2(sevensegment2_1_s2), .s3(sevensegment2_1_s3), .s4(sevensegment2_1_s4),
    .s5(sevensegment2_1_s5), .s6(sevensegment2_1_s6), .s7(sevensegment2_1_s7));
  sevensements1 sevensements1_2 (
    .i1(counter_2_q[4]), .i2(counter_2_q[3]), .i3(counter_2_q[2]), .i4(counter_2_q[1]), .i5(counter_2_q[0]),
    .s1(sevensements1_2_s1), .s2(sevensements1_2_s2), .s3(sevensements1_2_s3), .s4(sevensements1_2_s4),
    .s5(sevensements1_2_s5), .s6(sevensements1_2_s6), .s7(sevensements1_2_s7));
  sevensegment2 sevensegment2_2 (
    .a(counter_2_q[4]), .b(counter_2_q[3]), .c(counter_2_q[2]), .d(counter_2_q[1]), .e(counter_2_q[0]),
    .s1(sevensegment2_2_s1), .s2(sevensegment2_2_s2), .s3(sevensegment2_2_s3), .s4(sevensegment2_2_s4),
    .s5(sevensegment2_2_s5), .s6(sevensegment2_2_s6), .s7(sevensegment2_2_s7));
  _7_Segment_Display #(.decimalPoint("false")) u_7_segment_display_1 (
    .g(sevensegment2_1_s1), .f(sevensegment2_1_s2), .a(sevensegment2_1_s3), .b(sevensegment2_1_s4),
    .e(sevensegment2_1_s7), .d(sevensegment2_1_s6), .c(sevensegment2_1_s5));
  _7_Segment_Display #(.decimalPoint("false")) u_7_segment_display_2 (
    .g(sevensegment2_2_s1), .f(sevensegment2_2_s2), .a(sevensegment2_2_s3), .b(sevensegment2_2_s4),
    .e(sevensegment2_2_s7), .d(sevensegment2_2_s6), .c(sevensegment2_2_s5));
  _7_Segment_Display #(.decimalPoint("false")) u_7_segment_display_3 (
    .g(sevensements1_1_s1), .f(sevensements1_1_s2), .a(sevensements1_1_s3), .b(sevensements1_1_s4),
    .e(sevensements1_1_s7), .d(sevensements1_1_s6), .c(sevensements1_1_s5));
  _7_Segment_Display #(.decimalPoint("false")) u_7_segment_display_4 (
    .g(sevensements1_2_s1), .f(sevensements1_2_s2), .a(sevensements1_2_s3), .b(sevensements1_2_s4),
    .e(sevensements1_2_s7), .d(sevensements1_2_s6), .c(sevensements1_2_s5));
  Comparator #(.mode("unsigned"), .width(5)) comparator_4 (
    .a(counter_2_q), .b(5'b10100), .gt(comparator_4_gt), .eq(comparator_4_eq), .lt(comparator_4_lt));
  Comparator #(.mode("unsigned"), .width(5)) comparator_5 (
    .a(counter_1_q), .b(5'b10100), .gt(comparator_5_gt), .eq(comparator_5_eq), .lt(comparator_5_lt));
  or or_1 (or_1_out, comparator_4_gt, comparator_4_eq);
  or or_2 (or_2_out, comparator_5_gt, comparator_5_eq);
  not not_1 (not_1_out, d_ff_1_qn);
  and and_3 (and_3_out, comparator_5_lt, not_1_out);
  and and_4 (and_4_out, or_2_out, not_1_out);
  LED led_1 (.in(and_3_out));
  LED led_2 (.in(and_4_out));
  LED led_3 (.in(and_5_out));
  LED led_4 (.in(and_6_out));
  and and_5 (and_5_out, not_2_out, comparator_4_lt);
  and and_6 (and_6_out, not_2_out, or_1_out);
  not not_2 (not_2_out, d_ff_1_q);
  LED led_5 (.in(d_ff_1_qn));
  LED led_6 (.in(d_ff_1_q));
endmodule

module sevensements1 (
  input  i1,
  input  i2,
  input  i3,
  input  i4,
  input  i5,
  output s1,
  output s2,
  output s3,
  output s4,
  output s5,
  output s6,
  output s7
);

  wire and_1_out, and_2_out, and_3_out, and_4_out, and_5_out, and_6_out, and_7_out, and_8_out, and_9_out,
       and_10_out, and_11_out, and_12_out, and_13_out, and_14_out, and_15_out, and_16_out, and_17_out,
       and_18_out, and_19_out, and_20_out, and_21_out, and_22_out, and_23_out, and_24_out, and_25_out,
       and_26_out, and_27_out, and_28_out, and_29_out, and_30_out, and_31_out, and_32_out, and_33_out,
       and_34_out, and_35_out, and_36_out, and_37_out, and_38_out, and_39_out, and_40_out, and_41_out,
       and_42_out, and_43_out, and_44_out, and_45_out, and_46_out, and_47_out, and_48_out, and_49_out,
       and_50_out, and_51_out, and_52_out, and_53_out, and_54_out, not_1_out, not_2_out, not_3_out,
       not_4_out, not_5_out;

  not not_1 (not_1_out, i1);
  not not_2 (not_2_out, i2);
  not not_3 (not_3_out, i3);
  not not_4 (not_4_out, i4);
  not not_5 (not_5_out, i5);
  and and_1 (and_1_out, not_2_out, not_3_out, i4);
  and and_2 (and_2_out, not_1_out, i3, not_4_out);
  and and_3 (and_3_out, i2, not_4_out);
  and and_4 (and_4_out, i1, not_3_out, not_5_out);
  and and_5 (and_5_out, not_1_out, i2, i3);
  and and_6 (and_6_out, i1, not_2_out, i4);
  and and_7 (and_7_out, not_2_out, i4, not_5_out);
  and and_8 (and_8_out, not_1_out, not_2_out, i3, not_4_out);
  and and_9 (and_9_out, i2, not_3_out, not_4_out);
  and and_10 (and_10_out, not_1_out, i2, i3, i4);
  and and_11 (and_11_out, i1, not_2_out, not_3_out, i4);
  and and_12 (and_12_out, i1, i2, not_4_out);
  and and_13 (and_13_out, not_2_out, not_4_out, not_5_out);
  and and_14 (and_14_out, i2, i4, not_5_out);
  and and_15 (and_15_out, not_1_out, not_2_out, i3, not_5_out);
  and and_16 (and_16_out, not_2_out, i4);
  and and_17 (and_17_out, not_1_out, i3, i5);
  and and_18 (and_18_out, i1, not_2_out, not_5_out);
  and and_19 (and_19_out, not_1_out, not_3_out, not_5_out);
  and and_20 (and_20_out, i1, not_3_out, i5);
  and and_21 (and_21_out, i2, not_4_out, i5);
  and and_22 (and_22_out, i2, i3, not_4_out);
  and and_23 (and_23_out, i1, i4, not_5_out);
  and and_24 (and_24_out, not_2_out, i4, i5);
  and and_25 (and_25_out, i2, not_4_out, not_5_out);
  and and_26 (and_26_out, not_3_out, i4, i5);
  and and_27 (and_27_out, i1, not_2_out, i5);
  and and_28 (and_28_out, i1, not_2_out, i4);
  and and_29 (and_29_out, not_1_out, not_3_out);
  and and_30 (and_30_out, i3, not_4_out, not_5_out);
  and and_31 (and_31_out, i2, i3, not_4_out);
  and and_32 (and_32_out, i2, i3, not_5_out);
  and and_33 (and_33_out, i1, not_3_out);
  and and_34 (and_34_out, not_2_out, i5);
  and and_35 (and_35_out, not_1_out, not_2_out, i3);
  and and_36 (and_36_out, not_3_out, not_4_out);
  and and_37 (and_37_out, i1, not_4_out);
  and and_38 (and_38_out, i2, i4, not_5_out);
  and and_39 (and_39_out, not_1_out, i5);
  and and_40 (and_40_out, not_2_out, not_3_out, i4);
  and and_41 (and_41_out, not_1_out, i3, not_4_out, i5);
  and and_42 (and_42_out, not_2_out, i4, not_5_out);
  and and_43 (and_43_out, not_1_out, i2, i3, i5);
  and and_44 (and_44_out, i1, not_2_out, i4);
  and and_45 (and_45_out, i2, not_4_out, i5);
  and and_46 (and_46_out, i1, not_2_out, not_5_out);
  and and_47 (and_47_out, not_1_out, not_3_out, not_5_out);
  and and_48 (and_48_out, i2, i3, not_4_out);
  and and_49 (and_49_out, i1, i4, not_5_out);
  and and_50 (and_50_out, not_2_out, i4, not_5_out);
  and and_51 (and_51_out, i1, not_2_out, not_5_out);
  and and_52 (and_52_out, not_1_out, not_3_out, not_5_out);
  and and_53 (and_53_out, i2, i3, not_4_out, not_5_out);
  and and_54 (and_54_out, i1, i4, not_5_out);
  or or_1 (s1, and_1_out, and_2_out, and_3_out, and_4_out, and_5_out, and_6_out, and_7_out);
  or or_2 (s2, and_8_out, and_9_out, and_10_out, and_11_out, and_12_out, and_13_out, and_14_out, and_15_out);
  or or_3 (s3, and_16_out, and_17_out, and_18_out, and_19_out, and_20_out, and_21_out, and_22_out, and_23_out);
  or or_4 (s4, and_24_out, and_25_out, and_26_out, and_27_out, and_28_out, and_29_out, and_30_out, and_31_out, and_32_out);
  or or_5 (s5, and_33_out, and_34_out, and_35_out, and_36_out, and_37_out, and_38_out, and_39_out);
  or or_6 (s7, and_50_out, and_51_out, and_52_out, and_53_out, and_54_out);
  or or_7 (s6, and_40_out, and_41_out, and_42_out, and_43_out, and_44_out, and_45_out, and_46_out, and_47_out, and_48_out, and_49_out);
endmodule

module sevensegment2 (
  input  a,
  input  b,
  input  c,
  input  d,
  input  e,
  output s1,
  output s2,
  output s3,
  output s4,
  output s5,
  output s6,
  output s7
);

  wire and_1_out, and_2_out, and_3_out, and_4_out, and_5_out, and_6_out, and_7_out, and_8_out, and_9_out,
       and_10_out, and_11_out, and_12_out, and_13_out, and_14_out, and_15_out, and_16_out, and_17_out,
       and_18_out, and_19_out, not_1_out, not_2_out, not_3_out, not_4_out;

  not not_1 (not_1_out, a);
  not not_2 (not_2_out, b);
  not not_3 (not_3_out, c);
  not not_4 (not_4_out, d);
  and and_1 (and_1_out, a, c);
  and and_2 (and_2_out, a, b);
  and and_3 (and_3_out, not_1_out, not_2_out);
  and and_4 (and_4_out, not_1_out, not_3_out, not_4_out);
  and and_5 (and_5_out, not_1_out, not_2_out);
  and and_6 (and_6_out, a, b);
  and and_7 (and_7_out, not_1_out, not_3_out, not_4_out);
  and and_8 (and_8_out, a, c);
  and and_9 (and_9_out, not_2_out, not_3_out);
  and and_10 (and_10_out, b, c, d);
  and and_11 (and_11_out, not_1_out, not_2_out);
  and and_12 (and_12_out, a, b);
  and and_13 (and_13_out, not_1_out, not_3_out, not_4_out);
  and and_14 (and_14_out, a, c);
  and and_15 (and_15_out, not_1_out, not_2_out);
  and and_16 (and_16_out, not_2_out, c);
  and and_17 (and_17_out, a, b, not_3_out);
  and and_18 (and_18_out, not_1_out, not_3_out, not_4_out);
  and and_19 (and_19_out, a, c, not_4_out);
  or or_1 (s1, and_1_out, and_2_out);
  or or_2 (s2, and_3_out, and_4_out);
  or or_3 (s3, and_5_out, and_6_out, and_7_out, and_8_out);
  or or_4 (s5, not_1_out, and_9_out, and_10_out);
  or or_5 (s6, and_11_out, and_12_out, and_13_out, and_14_out);
  or or_6 (s7, and_15_out, and_16_out, and_17_out, and_18_out, and_19_out);

  assign s4 = 1'b1;
endmodule

module sevensegments (
  input  i0,
  input  i1,
  input  i2,
  input  i3,
  output s7,
  output s6,
  output s5,
  output s4,
  output s3,
  output s2,
  output s1
);

  wire and_1_out, and_2_out, and_3_out, and_4_out, and_5_out, and_6_out, and_7_out, and_8_out, and_9_out,
       and_10_out, and_11_out, and_12_out, and_13_out, and_14_out, and_15_out, and_16_out, not_1_out,
       not_2_out, not_3_out;

  not not_1 (not_1_out, i1);
  not not_2 (not_2_out, i2);
  not not_3 (not_3_out, i3);
  and and_1 (and_1_out, not_1_out, i2);
  and and_2 (and_2_out, i1, not_2_out);
  and and_3 (and_3_out, i2, not_3_out);
  and and_4 (and_4_out, not_2_out, not_3_out);
  and and_5 (and_5_out, i1, not_2_out);
  and and_6 (and_6_out, i1, not_3_out);
  and and_7 (and_7_out, not_1_out, not_3_out);
  and and_8 (and_8_out, i2, not_3_out);
  and and_9 (and_9_out, not_1_out, not_3_out);
  and and_10 (and_10_out, not_1_out, i2);
  and and_11 (and_11_out, i1, not_2_out, i3);
  and and_12 (and_12_out, i2, not_3_out);
  or or_1 (s3, not_2_out, i3, i1);
  and and_13 (and_13_out, not_2_out, not_3_out);
  and and_14 (and_14_out, i2, i3);
  and and_15 (and_15_out, not_1_out, not_3_out);
  and and_16 (and_16_out, i1, i3);
  or or_2 (s7, and_1_out, and_2_out, i0, and_3_out);
  or or_3 (s6, and_4_out, and_5_out, and_6_out, i0);
  or or_4 (s5, and_7_out, and_8_out);
  or or_5 (s4, and_9_out, and_10_out, and_11_out, and_12_out, i0);
  or or_6 (s2, not_1_out, and_13_out, and_14_out);
  or or_7 (s1, and_15_out, i2, and_16_out, i0);
endmodule
